# Fritzing sketch fys_project (saved by Fritzing 0.9.10b)
breadboards: 1

parts:
  J1 = Basic Servo
  HC-SR04_Sensor_1 = HC-SR04 Ultrasonic Distance Sensor
  Mod1 = KY-008 Laser Transmitter Module [package="Breakout board"]
  Mod2 = KY-018 Photoresistor Module [package="Breakout board"]
  Part1 = ODROID-N2Plus [part_number="ODROID N2Plus"]
  Mod3 = KY-026 Flame Sensor Module [package="Breakout board"]
  U1 = 7-SEGMENT-4DIGIT [package=7-segment-4digit]
  R1 = Resistor [tolerance=±5% resistance=220 package="1206 [SMD]"]
  R2 = Resistor [tolerance=±5% resistance=220 package="1206 [SMD]"]
  R4 = Resistor [tolerance=±5% resistance=220 package="1206 [SMD]"]
  R5 = Resistor [tolerance=±5% resistance=220 package="1206 [SMD]"]
  R8 = Resistor [tolerance=±5% resistance=220 package="1206 [SMD]"]
  R10 = Resistor [tolerance=±5% resistance=220 package="1206 [SMD]"]
  R13 = Resistor [tolerance=±5% resistance=220 package="1206 [SMD]"]

nets:
  GND: J1.gnd, HC-SR04_Sensor_1.GND, Mod1.NC, Mod1.-, Mod2.-, Part1.connector6, Mod3.G
  VCC: J1.vcc, HC-SR04_Sensor_1.VCC, Mod1.S, Part1.connector2, Mod3.+
  N1: J1.pulse, Part1.connector14
  N2: HC-SR04_Sensor_1.TRIG, Part1.connector7
  N3: HC-SR04_Sensor_1.ECHO, Part1.connector11
  N4: Mod2.S, Part1.connector5
  N5: Mod2.Vin, Part1.connector1
  N6: Part1.connector13, R1.Pin_1
  N7: Part1.connector15, R2.Pin_1
  N8: Part1.connector16, R4.Pin_1
  N9: Part1.connector18, R5.Pin_1
  N10: Part1.connector22, U1.13
  N11: Part1.connector29, R13.Pin_0
  N12: Part1.connector31, R10.Pin_0
  N13: Part1.connector33, R8.Pin_0
  N14: Part1.connector35, U1.16
  N15: Part1.connector40, Mod3.A0

custom parts:
  KY-008 Laser Transmitter Module: KY-008 Laser Transmitter Module, emits a dot shaped red laser beam.
  KY-018 Photoresistor Module: KY-018 Photoresistor module, used to measure light intensity. It can determine the presence or absence of light.
  KY-026 Flame Sensor Module: KY-026 Flame Sensor Module reacts in the presence of fire.
